// Logisim project stack_logical.circ as structural Verilog: 19 circuits, main circuit main
module main (
  input  CLK,
  input  RESET,
  input  [1:0] COMMAND,
  input  [2:0] INDEX,
  input  [3:0] IO_DATA_in,
  output [3:0] IO_DATA_out
);

  wire [3:0] stack_1_d0, stack_1_d1, stack_1_d2, stack_1_d3, stack_1_d4;

  // Probe on stack_1_d0
  stack stack_1 (
    .CLK(CLK), .RESET(RESET), .COMMAND(COMMAND), .INDEX(INDEX), .IO_DATA_in(IO_DATA_in), .d0(stack_1_d0),
    .d1(stack_1_d1), .d2(stack_1_d2), .d3(stack_1_d3), .d4(stack_1_d4), .IO_DATA_out(IO_DATA_out));
  // Probe on stack_1_d1
  // Probe on stack_1_d2
  // Probe on stack_1_d3
  // Probe on stack_1_d4
endmodule

module stack (
  input  CLK,
  input  RESET,
  input  [1:0] COMMAND,
  input  [2:0] INDEX,
  input  [3:0] IO_DATA_in,
  output [3:0] d0,
  output [3:0] d1,
  output [3:0] d2,
  output [3:0] d3,
  output [3:0] d4,
  output [3:0] IO_DATA_out
);

  wire and_2_out, and_3_out, and_4_out, and_5_out, and_6_out, get, GetPointer0, GetPointer1, GetPointer2,
       IsRead, MemCell0, MemCell1, MemCell2, minusminus_1_i0minus, minusminus_1_i1minus,
       minusminus_1_i2minus, NewTop0, NewTop1, NewTop2, nop, not_1_out, not_2_out, not_3_out, not_4_out,
       not_5_out, not_6_out, not_7_out, not_8_out, not_9_out, not_10_out, O0, O1, O2, O3, OldTop0, OldTop1,
       OldTop2, or_1_out, pop, PopPointer0, PopPointer1, PopPointer2, push, PushPointer0, PushPointer1,
       PushPointer2, threebitsubstructor_1_o0, threebitsubstructor_1_o1, threebitsubstructor_1_o2;

  or or_1 (or_1_out, pop, get);
  and and_1 (IsRead, CLK, or_1_out);
  TopUpdate topupdate_1 (
    .Operation0(COMMAND[0]), .Operation1(COMMAND[1]), .Reset(RESET), .C(CLK), .NewTop0(NewTop0),
    .NewTop1(NewTop1), .NewTop2(NewTop2), .OldTop0(OldTop0), .OldTop1(OldTop1), .OldTop2(OldTop2));
  CommandParser commandparser_1 (
    .Command0(COMMAND[0]), .Command1(COMMAND[1]), .nop(nop), .push(push), .pop(pop), .get(get));
  ConditionalOperator conditionaloperator_1 (
    .I0(OldTop0), .I1(OldTop1), .I2(OldTop2), .BoolFlag(push), .O0(PushPointer0), .O1(PushPointer1),
    .O2(PushPointer2));
  ConditionalOperator conditionaloperator_2 (
    .I0(NewTop0), .I1(NewTop1), .I2(NewTop2), .BoolFlag(pop), .O0(PopPointer0), .O1(PopPointer1),
    .O2(PopPointer2));
  ThreeBitSubstructor threebitsubstructor_1 (
    .Cur0(NewTop0), .Cur1(NewTop1), .Cur2(NewTop2), .Sub0(INDEX[0]), .Sub1(INDEX[1]), .Sub2(INDEX[2]),
    .O0(threebitsubstructor_1_o0), .O1(threebitsubstructor_1_o1), .O2(threebitsubstructor_1_o2));
  MinusMinus minusminus_1 (
    .I0(threebitsubstructor_1_o0), .I1(threebitsubstructor_1_o1), .I2(threebitsubstructor_1_o2),
    .I0Minus(minusminus_1_i0minus), .I1Minus(minusminus_1_i1minus), .I2Minus(minusminus_1_i2minus));
  or or_2 (MemCell0, PushPointer0, PopPointer0, GetPointer0);
  or or_3 (MemCell1, PushPointer1, PopPointer1, GetPointer1);
  or or_4 (MemCell2, PushPointer2, PopPointer2, GetPointer2);
  ConditionalOperator conditionaloperator_3 (
    .I0(minusminus_1_i0minus), .I1(minusminus_1_i1minus), .I2(minusminus_1_i2minus), .BoolFlag(get),
    .O0(GetPointer0), .O1(GetPointer1), .O2(GetPointer2));
  // Probe on IO_DATA_in[0]
  Memory MainMemory (
    .I0(MemCell0), .I1(MemCell1), .I2(MemCell2), .IsWrite(push), .C(CLK), .D0(IO_DATA_in[0]),
    .D1(IO_DATA_in[1]), .D2(IO_DATA_in[2]), .D3(IO_DATA_in[3]), .Reset(RESET), .O0(O0), .O1(O1), .O2(O2),
    .O3(O3));
  IOParser ioparser_1 (
    .IsRead(IsRead), .DataBit0(O0), .DataBit1(O1), .DataBit2(O2), .DataBit3(O3), .OutputBit0(IO_DATA_in[0]),
    .OutputBit1(IO_DATA_in[1]), .OutputBit2(IO_DATA_in[2]), .OutputBit3(IO_DATA_in[3]));
  not not_1 (not_1_out, MemCell0);
  not not_2 (not_2_out, MemCell1);
  not not_3 (not_3_out, MemCell2);
  and and_2 (and_2_out, not_1_out, not_2_out, not_3_out);
  not not_4 (not_4_out, MemCell1);
  not not_5 (not_5_out, MemCell2);
  and and_3 (and_3_out, MemCell0, not_4_out, not_5_out);
  not not_6 (not_6_out, MemCell0);
  not not_7 (not_7_out, MemCell2);
  and and_4 (and_4_out, not_6_out, MemCell1, not_7_out);
  not not_8 (not_8_out, MemCell2);
  StackElementOutHelper stackelementouthelper_1 (
    .O0(O0), .O1(O1), .O2(O2), .O3(O3), .IsCurrent(and_2_out), .push(push), .CLK(CLK), .RESET(RESET),
    .dx0(d0[0]), .dx1(d0[1]), .dx2(d0[2]), .dx3(d0[3]));
  and and_5 (and_5_out, MemCell0, MemCell1, not_8_out);
  StackElementOutHelper stackelementouthelper_2 (
    .O0(O0), .O1(O1), .O2(O2), .O3(O3), .IsCurrent(and_3_out), .push(push), .CLK(CLK), .RESET(RESET),
    .dx0(d1[0]), .dx1(d1[1]), .dx2(d1[2]), .dx3(d1[3]));
  not not_9 (not_9_out, MemCell0);
  not not_10 (not_10_out, MemCell1);
  and and_6 (and_6_out, not_9_out, not_10_out, MemCell2);
  StackElementOutHelper stackelementouthelper_3 (
    .O0(O0), .O1(O1), .O2(O2), .O3(O3), .IsCurrent(and_4_out), .push(push), .CLK(CLK), .RESET(RESET),
    .dx0(d2[0]), .dx1(d2[1]), .dx2(d2[2]), .dx3(d2[3]));
  StackElementOutHelper stackelementouthelper_4 (
    .O0(O0), .O1(O1), .O2(O2), .O3(O3), .IsCurrent(and_5_out), .push(push), .CLK(CLK), .RESET(RESET),
    .dx0(d3[0]), .dx1(d3[1]), .dx2(d3[2]), .dx3(d3[3]));
  StackElementOutHelper stackelementouthelper_5 (
    .O0(O0), .O1(O1), .O2(O2), .O3(O3), .IsCurrent(and_6_out), .push(push), .CLK(CLK), .RESET(RESET),
    .dx0(d4[0]), .dx1(d4[1]), .dx2(d4[2]), .dx3(d4[3]));

  assign IO_DATA_out = IO_DATA_in;

  // Other names for the same wires on the sheet: InputBit0 = IO_DATA_in[0]; OutputBit0 = IO_DATA_in[0];
  //   InputBit1 = IO_DATA_in[1]; OutputBit1 = IO_DATA_in[1]; InputBit2 = IO_DATA_in[2]; OutputBit2 = IO_DATA_in[2];
  //   InputBit3 = IO_DATA_in[3]; OutputBit3 = IO_DATA_in[3]
endmodule

module DTrigger (
  input  C,
  input  D,
  output Q
);

  wire and_1_out, and_2_out, not_1_out;

  not not_1 (not_1_out, D);
  and and_1 (and_1_out, C, not_1_out);
  and and_2 (and_2_out, C, D);
  RSTrigger rstrigger_1 (.R(and_1_out), .S(and_2_out), .Q(Q));
endmodule

module RSTrigger (
  input  R,
  input  S,
  output Q
);

  wire nor_2_out, or_1_out, por_1_out;

  nor nor_1 (Q, R, or_1_out);
  nor nor_2 (nor_2_out, Q, S);
  POR por_1 (.out(por_1_out));
  or or_1 (or_1_out, nor_2_out, por_1_out);
endmodule

module FourBitMemoryCell (
  input  D0,
  input  D1,
  input  D2,
  input  D3,
  input  Reset,
  input  C,
  output Q0,
  output Q1,
  output Q2,
  output Q3
);

  wire and_1_out, and_2_out, and_3_out, and_4_out, not_1_out, or_1_out;

  not not_1 (not_1_out, Reset);
  and and_1 (and_1_out, D0, not_1_out);
  and and_2 (and_2_out, D1, not_1_out);
  and and_3 (and_3_out, D2, not_1_out);
  and and_4 (and_4_out, D3, not_1_out);
  or or_1 (or_1_out, Reset, C);
  DTrigger dtrigger_1 (.C(or_1_out), .D(and_1_out), .Q(Q0));
  DTrigger dtrigger_2 (.C(or_1_out), .D(and_2_out), .Q(Q1));
  DTrigger dtrigger_3 (.C(or_1_out), .D(and_3_out), .Q(Q2));
  DTrigger dtrigger_4 (.C(or_1_out), .D(and_4_out), .Q(Q3));
endmodule

module ThreeBitsToDecMod (
  input  I0,
  input  I1,
  input  I2,
  output O0,
  output O1,
  output O2,
  output O3,
  output O4
);

  wire and_1_out, and_2_out, and_3_out, and_4_out, and_5_out, and_6_out, not_1_out, not_2_out, not_3_out,
       not_4_out, not_5_out, not_6_out, not_7_out, not_8_out, not_9_out, not_10_out, not_11_out, not_12_out;

  not not_1 (not_1_out, I0);
  not not_2 (not_2_out, I1);
  not not_3 (not_3_out, I2);
  not not_4 (not_4_out, I1);
  not not_5 (not_5_out, I1);
  not not_6 (not_6_out, I2);
  not not_7 (not_7_out, I0);
  not not_8 (not_8_out, I0);
  not not_9 (not_9_out, I2);
  not not_10 (not_10_out, I2);
  not not_11 (not_11_out, I0);
  not not_12 (not_12_out, I1);
  and and_1 (and_1_out, not_1_out, not_2_out, not_3_out);
  and and_2 (and_2_out, I0, not_4_out, I2);
  and and_3 (and_3_out, I0, not_5_out, not_6_out);
  and and_4 (and_4_out, not_7_out, I1, I2);
  and and_5 (and_5_out, not_8_out, I1, not_9_out);
  and and_6 (and_6_out, I0, I1, I2);
  and and_7 (O3, I0, I1, not_10_out);
  and and_8 (O4, not_11_out, not_12_out, I2);
  or or_1 (O0, and_1_out, and_2_out);
  or or_2 (O1, and_3_out, and_4_out);
  or or_3 (O2, and_5_out, and_6_out);
endmodule

module DecModToThreeBits (
  input  O0,
  input  O1,
  input  O2,
  input  O3,
  input  O4,
  output I0,
  output I1,
  output I2
);

  or or_1 (I0, O1, O3);
  or or_2 (I1, O2, O3);

  assign I2 = O4;
endmodule

module MemoryLogic (
  input  I0,
  input  I1,
  input  I2,
  input  Cell00,
  input  Cell01,
  input  Cell02,
  input  Cell03,
  input  Cell10,
  input  Cell11,
  input  Cell12,
  input  Cell13,
  input  Cell20,
  input  Cell21,
  input  Cell22,
  input  Cell23,
  input  Cell30,
  input  Cell31,
  input  Cell32,
  input  Cell33,
  input  Cell40,
  input  Cell41,
  input  Cell42,
  input  Cell43,
  output O0,
  output O1,
  output O2,
  output O3
);

  wire Flag00, Flag01, Flag02, Flag03, Flag10, Flag11, Flag12, Flag13, Flag20, Flag21, Flag22, Flag23,
       Flag30, Flag31, Flag32, Flag33, Flag40, Flag41, Flag42, Flag43, Value0, Value1, Value2, Value3, Value4;

  ThreeBitsToDecMod threebitstodecmod_1 (
    .I0(I0), .I1(I1), .I2(I2), .O0(Value0), .O1(Value1), .O2(Value2), .O3(Value3), .O4(Value4));
  and and_1 (Flag00, Cell00, Value0);
  and and_2 (Flag01, Cell01, Value0);
  and and_3 (Flag02, Cell02, Value0);
  and and_4 (Flag03, Cell03, Value0);
  and and_5 (Flag10, Cell10, Value1);
  and and_6 (Flag11, Cell11, Value1);
  and and_7 (Flag12, Cell12, Value1);
  and and_8 (Flag13, Cell13, Value1);
  and and_9 (Flag20, Cell20, Value2);
  and and_10 (Flag21, Cell21, Value2);
  and and_11 (Flag22, Cell22, Value2);
  and and_12 (Flag23, Cell23, Value2);
  and and_13 (Flag30, Cell30, Value3);
  and and_14 (Flag31, Cell31, Value3);
  and and_15 (Flag32, Cell32, Value3);
  and and_16 (Flag33, Cell33, Value3);
  and and_17 (Flag40, Cell40, Value4);
  and and_18 (Flag41, Cell41, Value4);
  and and_19 (Flag42, Cell42, Value4);
  and and_20 (Flag43, Cell43, Value4);
  or or_1 (O0, Flag00, Flag10, Flag20, Flag30, Flag40);
  or or_2 (O1, Flag01, Flag11, Flag21, Flag31, Flag41);
  or or_3 (O2, Flag02, Flag12, Flag22, Flag32, Flag42);
  or or_4 (O3, Flag03, Flag13, Flag23, Flag33, Flag43);

  // Notes on the sheet:
  //   Возвращаем данные из ячейки памяти по её номеру
endmodule

module Memory (
  input  I0,
  input  I1,
  input  I2,
  input  IsWrite,
  input  C,
  input  D0,
  input  D1,
  input  D2,
  input  D3,
  input  Reset,
  output O0,
  output O1,
  output O2,
  output O3
);

  wire and_1_out, Cell00, Cell01, Cell02, Cell03, Cell10, Cell11, Cell12, Cell13, Cell20, Cell21, Cell22,
       Cell23, Cell30, Cell31, Cell32, Cell33, Cell40, Cell41, Cell42, Cell43, threebitstodecmod_1_o0,
       threebitstodecmod_1_o1, threebitstodecmod_1_o2, threebitstodecmod_1_o3, threebitstodecmod_1_o4,
       Value0, Value1, Value2, Value3, Value4;

  and and_1 (and_1_out, IsWrite, C);
  ThreeBitsToDecMod threebitstodecmod_1 (
    .I0(I0), .I1(I1), .I2(I2), .O0(threebitstodecmod_1_o0), .O1(threebitstodecmod_1_o1),
    .O2(threebitstodecmod_1_o2), .O3(threebitstodecmod_1_o3), .O4(threebitstodecmod_1_o4));
  and and_2 (Value0, threebitstodecmod_1_o0, and_1_out);
  and and_3 (Value1, threebitstodecmod_1_o1, and_1_out);
  and and_4 (Value2, threebitstodecmod_1_o2, and_1_out);
  and and_5 (Value3, threebitstodecmod_1_o3, and_1_out);
  and and_6 (Value4, threebitstodecmod_1_o4, and_1_out);
  FourBitMemoryCell fourbitmemorycell_1 (
    .D0(D0), .D1(D1), .D2(D2), .D3(D3), .Reset(Reset), .C(Value0), .Q0(Cell00), .Q1(Cell01), .Q2(Cell02),
    .Q3(Cell03));
  FourBitMemoryCell fourbitmemorycell_2 (
    .D0(D0), .D1(D1), .D2(D2), .D3(D3), .Reset(Reset), .C(Value1), .Q0(Cell10), .Q1(Cell11), .Q2(Cell12),
    .Q3(Cell13));
  FourBitMemoryCell fourbitmemorycell_3 (
    .D0(D0), .D1(D1), .D2(D2), .D3(D3), .Reset(Reset), .C(Value2), .Q0(Cell20), .Q1(Cell21), .Q2(Cell22),
    .Q3(Cell23));
  FourBitMemoryCell fourbitmemorycell_4 (
    .D0(D0), .D1(D1), .D2(D2), .D3(D3), .Reset(Reset), .C(Value3), .Q0(Cell30), .Q1(Cell31), .Q2(Cell32),
    .Q3(Cell33));
  FourBitMemoryCell fourbitmemorycell_5 (
    .D0(D0), .D1(D1), .D2(D2), .D3(D3), .Reset(Reset), .C(Value4), .Q0(Cell40), .Q1(Cell41), .Q2(Cell42),
    .Q3(Cell43));
  MemoryLogic memorylogic_1 (
    .I0(I0), .I1(I1), .I2(I2), .Cell00(Cell00), .Cell01(Cell01), .Cell02(Cell02), .Cell03(Cell03),
    .Cell10(Cell10), .Cell11(Cell11), .Cell12(Cell12), .Cell13(Cell13), .Cell20(Cell20), .Cell21(Cell21),
    .Cell22(Cell22), .Cell23(Cell23), .Cell30(Cell30), .Cell31(Cell31), .Cell32(Cell32), .Cell33(Cell33),
    .Cell40(Cell40), .Cell41(Cell41), .Cell42(Cell42), .Cell43(Cell43), .O0(O0), .O1(O1), .O2(O2), .O3(O3));

  // Notes on the sheet:
  //   Чтение из памяти, запись в неё
endmodule

module PlusPlus (
  input  I0,
  input  I1,
  input  I2,
  output I0Plus,
  output I1Plus,
  output I2Plus
);

  wire O0, O1, O2, O3, O4;

  ThreeBitsToDecMod threebitstodecmod_1 (.I0(I0), .I1(I1), .I2(I2), .O0(O0), .O1(O1), .O2(O2), .O3(O3), .O4(O4));
  DecModToThreeBits decmodtothreebits_1 (
    .O0(O4), .O1(O0), .O2(O1), .O3(O2), .O4(O3), .I0(I0Plus), .I1(I1Plus), .I2(I2Plus));
endmodule

module MinusMinus (
  input  I0,
  input  I1,
  input  I2,
  output I0Minus,
  output I1Minus,
  output I2Minus
);

  wire O0, O1, O2, O3, O4;

  ThreeBitsToDecMod threebitstodecmod_1 (.I0(I0), .I1(I1), .I2(I2), .O0(O0), .O1(O1), .O2(O2), .O3(O3), .O4(O4));
  DecModToThreeBits decmodtothreebits_1 (
    .O0(O1), .O1(O2), .O2(O3), .O3(O4), .O4(O0), .I0(I0Minus), .I1(I1Minus), .I2(I2Minus));
endmodule

module ThreeBitSubstructor (
  input  Cur0,
  input  Cur1,
  input  Cur2,
  input  Sub0,
  input  Sub1,
  input  Sub2,
  output O0,
  output O1,
  output O2
);

  wire and_1_out, and_2_out, and_3_out, and_4_out, and_5_out, and_6_out, and_7_out, and_8_out, and_9_out,
       and_10_out, and_11_out, and_12_out, and_13_out, and_14_out, and_15_out, Cur0Minus1, Cur0Minus2,
       Cur0Minus3, Cur0Minus4, Cur1Minus1, Cur1Minus2, Cur1Minus3, Cur1Minus4, Cur2Minus1, Cur2Minus2,
       Cur2Minus3, Cur2Minus4, IsSub0, IsSub1, IsSub2, IsSub3, IsSub4;

  ThreeBitsToDecMod threebitstodecmod_1 (
    .I0(Sub0), .I1(Sub1), .I2(Sub2), .O0(IsSub0), .O1(IsSub1), .O2(IsSub2), .O3(IsSub3), .O4(IsSub4));
  MinusMinus minusminus_1 (
    .I0(Cur0), .I1(Cur1), .I2(Cur2), .I0Minus(Cur0Minus1), .I1Minus(Cur1Minus1), .I2Minus(Cur2Minus1));
  MinusMinus minusminus_2 (
    .I0(Cur0Minus1), .I1(Cur1Minus1), .I2(Cur2Minus1), .I0Minus(Cur0Minus2), .I1Minus(Cur1Minus2),
    .I2Minus(Cur2Minus2));
  MinusMinus minusminus_3 (
    .I0(Cur0Minus2), .I1(Cur1Minus2), .I2(Cur2Minus2), .I0Minus(Cur0Minus3), .I1Minus(Cur1Minus3),
    .I2Minus(Cur2Minus3));
  MinusMinus minusminus_4 (
    .I0(Cur0Minus3), .I1(Cur1Minus3), .I2(Cur2Minus3), .I0Minus(Cur0Minus4), .I1Minus(Cur1Minus4),
    .I2Minus(Cur2Minus4));
  and and_1 (and_1_out, Cur0, IsSub0);
  and and_2 (and_2_out, Cur0Minus1, IsSub1);
  and and_3 (and_3_out, Cur0Minus2, IsSub2);
  and and_4 (and_4_out, Cur0Minus3, IsSub3);
  and and_5 (and_5_out, Cur0Minus4, IsSub4);
  or or_1 (O0, and_1_out, and_2_out, and_3_out, and_4_out, and_5_out);
  and and_6 (and_6_out, Cur1, IsSub0);
  and and_7 (and_7_out, Cur1Minus1, IsSub1);
  and and_8 (and_8_out, Cur1Minus2, IsSub2);
  and and_9 (and_9_out, Cur1Minus3, IsSub3);
  and and_10 (and_10_out, Cur1Minus4, IsSub4);
  or or_2 (O1, and_6_out, and_7_out, and_8_out, and_9_out, and_10_out);
  and and_11 (and_11_out, Cur2, IsSub0);
  and and_12 (and_12_out, Cur2Minus1, IsSub1);
  and and_13 (and_13_out, Cur2Minus2, IsSub2);
  and and_14 (and_14_out, Cur2Minus3, IsSub3);
  and and_15 (and_15_out, Cur2Minus4, IsSub4);
  or or_3 (O2, and_11_out, and_12_out, and_13_out, and_14_out, and_15_out);

  // Notes on the sheet:
  //   У нас есть надёжная протестированная операция --. Поэтому мы можем сделать её Sub2Sub1Sub0 раз! 
endmodule

module TopTransform (
  input  Top0,
  input  Top1,
  input  Top2,
  input  Operation0,
  input  Operation1,
  input  Reset,
  output NewTop0,
  output NewTop1,
  output NewTop2
);

  wire and_1_out, and_2_out, and_3_out, and_4_out, and_5_out, and_6_out, and_7_out, and_8_out, and_9_out,
       MinusTop0, MinusTop1, MinusTop2, not_2_out, not_3_out, not_4_out, not_5_out, not_6_out, not_7_out,
       not_8_out, not_9_out, not_10_out, NotReset, PlusTop0, PlusTop1, PlusTop2, TempTop0, TempTop1,
       TempTop2, xor_1_out, xor_2_out, xor_3_out;

  not not_1 (NotReset, Reset);
  PlusPlus plusplus_1 (.I0(Top0), .I1(Top1), .I2(Top2), .I0Plus(PlusTop0), .I1Plus(PlusTop1), .I2Plus(PlusTop2));
  MinusMinus minusminus_1 (
    .I0(Top0), .I1(Top1), .I2(Top2), .I0Minus(MinusTop0), .I1Minus(MinusTop1), .I2Minus(MinusTop2));
  xor xor_1 (xor_1_out, Operation0, Operation1);
  not not_2 (not_2_out, Operation1);
  not not_3 (not_3_out, Operation0);
  xor xor_2 (xor_2_out, Operation0, Operation1);
  not not_4 (not_4_out, Operation1);
  not not_5 (not_5_out, Operation0);
  xor xor_3 (xor_3_out, Operation0, Operation1);
  not not_6 (not_6_out, Operation1);
  not not_7 (not_7_out, Operation0);
  not not_8 (not_8_out, xor_1_out);
  and and_1 (and_1_out, not_8_out, Top0);
  and and_2 (and_2_out, Operation0, not_2_out, PlusTop0);
  and and_3 (and_3_out, not_3_out, Operation1, MinusTop0);
  not not_9 (not_9_out, xor_2_out);
  and and_4 (and_4_out, not_9_out, Top1);
  and and_5 (and_5_out, Operation0, not_4_out, PlusTop1);
  and and_6 (and_6_out, not_5_out, Operation1, MinusTop1);
  not not_10 (not_10_out, xor_3_out);
  and and_7 (and_7_out, not_10_out, Top2);
  and and_8 (and_8_out, Operation0, not_6_out, PlusTop2);
  and and_9 (and_9_out, not_7_out, Operation1, MinusTop2);
  or or_1 (TempTop0, and_1_out, and_2_out, and_3_out);
  or or_2 (TempTop1, and_4_out, and_5_out, and_6_out);
  or or_3 (TempTop2, and_7_out, and_8_out, and_9_out);
  and and_10 (NewTop0, TempTop0, NotReset);
  and and_11 (NewTop1, TempTop1, NotReset);
  and and_12 (NewTop2, TempTop2, NotReset);

  // Notes on the sheet:
  //   Если Operation = 01 - top++ (push)
  //   Если Operation = 10 - top-- (pop)
  //   Если Reset = 1 - обнуляем вершину стека
  //   Если Operation = 11 или 00 - оставляем top без изменений (nop / get)
  //   Top - индекс, следующий за индексом последней заполненной ячейки
endmodule

module TopUpdate (
  input  Operation0,
  input  Operation1,
  input  Reset,
  input  C,
  output NewTop0,
  output NewTop1,
  output NewTop2,
  output OldTop0,
  output OldTop1,
  output OldTop2
);

  wire NewC, not_1_out, TempNewTop0, TempNewTop1, TempNewTop2, UpdateC;

  not not_1 (not_1_out, C);
  or or_1 (NewC, Reset, C);
  or or_2 (UpdateC, Reset, not_1_out);
  TopTransform toptransform_1 (
    .Top0(OldTop0), .Top1(OldTop1), .Top2(OldTop2), .Operation0(Operation0), .Operation1(Operation1),
    .Reset(Reset), .NewTop0(TempNewTop0), .NewTop1(TempNewTop1), .NewTop2(TempNewTop2));
  DTrigger dtrigger_1 (.C(NewC), .D(TempNewTop0), .Q(NewTop0));
  DTrigger dtrigger_2 (.C(NewC), .D(TempNewTop1), .Q(NewTop1));
  DTrigger dtrigger_3 (.C(NewC), .D(TempNewTop2), .Q(NewTop2));
  DTrigger dtrigger_4 (.C(UpdateC), .D(NewTop0), .Q(OldTop0));
  DTrigger dtrigger_5 (.C(UpdateC), .D(NewTop1), .Q(OldTop1));
  DTrigger dtrigger_6 (.C(UpdateC), .D(NewTop2), .Q(OldTop2));

  // Notes on the sheet:
  //   2
  //   Проходимся по циклу 1-2-3-1 при включении и выключении синхронизации
  //   3
  //   1
endmodule

module ConditionalOperator (
  input  I0,
  input  I1,
  input  I2,
  input  BoolFlag,
  output O0,
  output O1,
  output O2
);

  and and_1 (O0, I0, BoolFlag);
  and and_2 (O1, I1, BoolFlag);
  and and_3 (O2, I2, BoolFlag);
endmodule

module IOBitParser (
  input  IsRead,
  input  DataBit,
  output OutputBit
);

  wire not_1_out;

  not not_1 (not_1_out, IsRead);
  // Transmission_Gate transmission_1: pin names not known; wires that end beside it: DataBit, not_1_out, IsRead, OutputBit
endmodule

module IOParser (
  input  IsRead,
  input  DataBit0,
  input  DataBit1,
  input  DataBit2,
  input  DataBit3,
  output OutputBit0,
  output OutputBit1,
  output OutputBit2,
  output OutputBit3
);

  IOBitParser iobitparser_1 (.IsRead(IsRead), .DataBit(DataBit0), .OutputBit(OutputBit0));
  IOBitParser iobitparser_2 (.IsRead(IsRead), .DataBit(DataBit1), .OutputBit(OutputBit1));
  IOBitParser iobitparser_3 (.IsRead(IsRead), .DataBit(DataBit2), .OutputBit(OutputBit2));
  IOBitParser iobitparser_4 (.IsRead(IsRead), .DataBit(DataBit3), .OutputBit(OutputBit3));
endmodule

module StackElementOutHelper (
  input  O0,
  input  O1,
  input  O2,
  input  O3,
  input  IsCurrent,
  input  push,
  input  CLK,
  input  RESET,
  output dx0,
  output dx1,
  output dx2,
  output dx3
);

  wire C, IsPush;

  and and_1 (IsPush, push, CLK);
  and and_2 (C, IsCurrent, IsPush);
  FourBitMemoryCell fourbitmemorycell_1 (
    .D0(O0), .D1(O1), .D2(O2), .D3(O3), .Reset(RESET), .C(C), .Q0(dx0), .Q1(dx1), .Q2(dx2), .Q3(dx3));
endmodule

module CommandParser (
  input  Command0,
  input  Command1,
  output nop,
  output push,
  output pop,
  output get
);

  wire not_1_out, not_2_out, not_3_out, not_4_out;

  not not_1 (not_1_out, Command0);
  not not_2 (not_2_out, Command1);
  not not_3 (not_3_out, Command1);
  not not_4 (not_4_out, Command0);
  and and_1 (nop, not_1_out, not_2_out);
  and and_2 (push, Command0, not_3_out);
  and and_3 (pop, not_4_out, Command1);
  and and_4 (get, Command0, Command1);
endmodule
